// Logisim project riscv_logisim.circ as structural Verilog: 6 circuits, main circuit main
module main (
  input  [31:0] in_1
);

  wire clock_1_out;

  Clock clock_1 (.out(clock_1_out));
  CPU cpu_1 (.Instruction(in_1), .Clk(clock_1_out));
endmodule

module CPU (
  input  [31:0] Instruction,
  input  Clk
);

  wire controllogic_1_regwe;
  wire [4:0] controllogic_1_regaddr;
  wire [31:0] controllogic_1_regdata;

  ControlLogic controllogic_1 (
    .Instruction(Instruction), .RegAddr(controllogic_1_regaddr), .RegWE(controllogic_1_regwe),
    .RegData(controllogic_1_regdata));  // open: PC
  RAM #(.addrWidth(5), .dataWidth(32), .enables("line")) Registers (
    .addr(controllogic_1_regaddr), .we(controllogic_1_regwe), .clk(Clk), .din(controllogic_1_regdata));  // open: dout
  Counter counter_1 ();  // open: clr, load, up, count, clk, D, carry, Q

  // Notes on the sheet:
  //   Registers
  //   PC
endmodule

module ControlLogic (
  input  [31:0] Instruction,
  input  [31:0] PC,
  output [4:0] RegAddr,
  output RegWE,
  output [31:0] RegData
);

  wire Is_AUIPC, IsLUI;
  wire [4:0] AUIPC_RegAddr, LUI_RegAddr;
  wire [31:0] AUIPC_RegData, LUI_RegData;

  LUI_Logic lui_logic_1 (.Instruction(Instruction), .IsLUI(IsLUI), .RD(LUI_RegAddr), .RegData(LUI_RegData));
  AUIPC_Logic auipc_logic_1 (
    .Instruction(Instruction), .PC(PC), .Is_AUIPC(Is_AUIPC), .RD(AUIPC_RegAddr), .RegData(AUIPC_RegData));
  assign RegAddr = LUI_RegAddr | AUIPC_RegAddr;  // OR_Gate or_1, 5 bits wide
  or or_2 (RegWE, IsLUI, Is_AUIPC);
  assign RegData = LUI_RegData | AUIPC_RegData;  // OR_Gate or_3, 32 bits wide
endmodule

module LUI_Logic (
  input  [31:0] Instruction,
  output IsLUI,
  output [4:0] RD,
  output [31:0] RegData
);

  wire [19:0] shifter_1_out;
  wire [31:0] bit_extender_1_out;

  Shifter #(.width(20)) shifter_1 (.in(Instruction[31:12]), .\dist (5'b01100), .out(shifter_1_out));
  assign bit_extender_1_out = {{12{shifter_1_out[19]}}, shifter_1_out};  // Bit_Extender bit_extender_1
  Comparator #(.width(7)) comparator_1 (.a(Instruction[6:0]), .b(7'b0110111), .eq(IsLUI));  // open: gt, lt
  Multiplexer #(.width(5)) multiplexer_1 (.in0({5{1'b0}}), .in1(Instruction[11:7]), .out(RD), .sel(IsLUI));
  Multiplexer #(.width(32)) multiplexer_2 (.in0({32{1'b0}}), .in1(bit_extender_1_out), .out(RegData), .sel(IsLUI));

  // Other names for the same wires on the sheet: LUI_Imm[19:0] = Instruction[31:12]
endmodule

module AUIPC_Logic (
  input  [31:0] Instruction,
  input  [31:0] PC,
  output Is_AUIPC,
  output [4:0] RD,
  output [31:0] RegData
);

  wire [19:0] shifter_1_out;
  wire [31:0] adder_1_out, bit_extender_1_out;

  Shifter #(.width(20)) shifter_1 (.in(Instruction[31:12]), .\dist (5'b01100), .out(shifter_1_out));
  assign bit_extender_1_out = {{12{shifter_1_out[19]}}, shifter_1_out};  // Bit_Extender bit_extender_1
  Multiplexer #(.width(5)) multiplexer_1 (.in0({5{1'b0}}), .in1(Instruction[11:7]), .out(RD), .sel(Is_AUIPC));
  Comparator #(.width(7)) comparator_1 (.a(Instruction[6:0]), .b(7'b0010111), .eq(Is_AUIPC));  // open: gt, lt
  Adder #(.width(32)) adder_1 (.a(bit_extender_1_out), .b(PC), .out(adder_1_out));  // open: cin, cout
  Multiplexer #(.width(32)) multiplexer_2 (.in0({32{1'b0}}), .in1(adder_1_out), .out(RegData), .sel(Is_AUIPC));

  // Other names for the same wires on the sheet: AUIPC_Imm[19:0] = Instruction[31:12]
endmodule

module ADDI_Logic (
  input  [31:0] Instruction,
  output Is_ADDI,
  output [4:0] RD,
  output [31:0] RegData
);

  wire Is_AUIPC;
  wire [19:0] shifter_1_out;
  wire [31:0] adder_1_out, bit_extender_1_out;

  Shifter #(.width(20)) shifter_1 (.in(Instruction[31:12]), .\dist (5'b01100), .out(shifter_1_out));
  assign bit_extender_1_out = {{12{shifter_1_out[19]}}, shifter_1_out};  // Bit_Extender bit_extender_1
  Comparator #(.width(7)) comparator_1 (.a(Instruction[6:0]), .b(7'b0010111), .eq(Is_ADDI));  // open: gt, lt
  Adder #(.width(32)) adder_1 (.a(bit_extender_1_out), .out(adder_1_out));  // open: b, cin, cout
  Multiplexer #(.width(5)) multiplexer_1 (.in0({5{1'b0}}), .in1(Instruction[11:7]), .out(RD), .sel(Is_ADDI));
  Multiplexer #(.width(32)) multiplexer_2 (.in0({32{1'b0}}), .in1(adder_1_out), .out(RegData), .sel(Is_AUIPC));

  // Other names for the same wires on the sheet: Imm[19:0] = Instruction[31:12]
endmodule
